# Fritzing sketch morse_encoder (saved by Fritzing 0.9.3b)
breadboards: 1

parts:
  LED1 = LED - 5mm [color="Yellow (595nm)" part_number=OUT_PIN package="5 mm [THT]"]
  Resistor_2 = Resistor [tolerance=±5% resistance=220 package=THT]
  Relay_1 = Relay [part_number=FRS1B-S package=THT]
  Relay_2 = Relay [part_number=FRS1B-S package=THT]
  LED2 = LED - 5mm [color="Red (633nm)" part_number=END_PIN package="5 mm [THT]"]
  Resistor_1 = Resistor [tolerance=±5% resistance=220 package=THT]
  part = ESP32S-DOIT [part_number=ESP32S-DOIT]

nets:
  N1: LED1.cathode, Resistor_1.Pin_1
  N2: LED1.anode, Relay_1.A
  N3: Resistor_2.Pin_0, Relay_1.COIL1, Relay_1.C1, Relay_1.C2, Relay_1.COIL2, Relay_2.COIL1, Relay_2.C1, Relay_2.C2, Relay_2.COIL2, Resistor_1.Pin_0, part.3.3, part.GND, part.GPIO23, part.GPIO22
  N4: Resistor_2.Pin_1, LED2.cathode
  N5: Relay_2.B, LED2.anode

custom parts:
  Relay: An SPDT relay.
  ESP32S-DOIT: DOIT ESP-WROOM-32 ESP32 ESP-32S Development Board 2.4GHz Dual-Mode WiFi + Bluetooth Dual Cores Microcontroller The ESP32 integrated with Antenna switches, RF Balun, power amplifiers, low-noise amplifiers, filters, and management modules, and the entire solution occupies the least area of PCB. 2.4 GHz Wi-Fi plus Bluetooth dual-mode chip, with TSMC Ultra-low power consumption 40nm technology,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
